# Fritzing sketch garage (saved by Fritzing 0.9.1b)
breadboards: 1

parts:
  Part1 = Arduino Micro (Rev3)
  S1 = Toggle Switch [package=THT]
  S2 = Pushbutton [package="[THT]"]
  PIR1 = PIR sensor
  J1 = Screw terminal - 2 pins [package=THT]
  U1 = Voltage Regulator - 5V [package="TO220 [THT]"]
  Q1 = NPN-Transistor [package="TO92 [THT]"]
  J2 = Piezo Speaker
  LED1 = LED - 5mm [color="Red (633nm)" package="5 mm [THT]"]
  S3 = Square Pushbutton
  R1 = Resistor [package="2010 [SMD]"]
  U2 = RELAY [package=relay-g5q]
  J3 = Screw terminal - 2 pins [package=THT]
  C1 = Capacitor Polarized [package=panasonic_h13]
  BATT1 = LiPoly Battery (1300mAh)
  M1 = DC Motor

nets:
  N1: Part1.D0/RX, S1.COM
  N2: Part1.D4_PWM/A6, J2.pin1
  N3: Part1.D5_PWM, Q1.B
  N4: Part1.D6_PWM/A7, U1.output_voltage
  GND: Part1.GND, S1.L2, U1.GND, J2.pin2, LED1.cathode, BATT1.negative
  N5: Part1.5V, S1.L1, S2.Pin_1, S2.Pin_2
  N6: Part1.D13_PWM, LED1.anode
  N7: S2.Pin_4, BATT1.positive
  N8: PIR1.VDD, C1.-
  N9: PIR1.SIG, U1.input_voltage
  N10: PIR1.GND, J1.pin1, S3.leg0, R1.Pin_0, C1.+
  N11: J1.pin2, Q1.E, U2.COIL2
  N12: Q1.C, R1.Pin_1
  N13: S3.leg1, U2.COIL1, J3.pin1, J3.pin2
  N14: U2.MAIN, M1.pin_2
  GND_2: U2.NO
  N15: U2.NC, M1.pin_1

custom parts:
  LiPoly Battery (1300mAh): Lithium Ion Polymer Battery (1300mAh)
