# Fritzing sketch garage2 (saved by Fritzing 0.9.1b)
circuit board: 8.46667cm x 5.64444cm
breadboards: 1

parts:
  Part1 = Arduino Micro (Rev3)
  S2 = Pushbutton [package="[THT]"]
  PIR1 = PIR sensor
  U1 = Voltage Regulator - 5V [package="TO220 [THT]"]
  Q1 = NPN-Transistor [package="TO92 [THT]"]
  R1 = Resistor [package="2010 [SMD]"]
  C1 = Capacitor Polarized [package=panasonic_h13]
  BATT1 = LiPoly Battery (1300mAh)
  JP1 = Header 4 [package=screwterminal-3.5mm-4_lock]
  U2 = RJ9 [package=rj9]

nets:
  N1: Part1.D0/RX, U2.2
  GND: Part1.GND, U1.GND, BATT1.negative, U2.3, U2.4
  N2: Part1.D5_PWM, Q1.B
  N3: Part1.D10_PWM/A10, U1.output_voltage
  N4: Part1.5V, S2.Pin_1, S2.Pin_2, U2.1
  N5: S2.Pin_4, BATT1.positive
  N6: PIR1.VDD, Q1.E, C1.-, JP1.2, JP1.3
  N7: PIR1.SIG, U1.input_voltage
  N8: PIR1.GND, Q1.C, R1.Pin_0, R1.Pin_1, C1.+, JP1.1, JP1.4

custom parts:
  LiPoly Battery (1300mAh): Lithium Ion Polymer Battery (1300mAh)
